# Fritzing sketch Nano_Lessons_Breadboard (saved by Fritzing 0.9.3b)
breadboards: 1

parts:
  Nano = Arduino Nano (Rev3.0)
  S1 = Pushbutton [package="[THT]"]
  S2 = Pushbutton [package="[THT]"]
  LED2 = LED - 5mm [color="Green (555nm)" package="5 mm [THT]"]
  LED3 = LED - 5mm [color="Yellow (595nm)" package="5 mm [THT]"]
  R11 = Resistor [tolerance=±5% resistance=270 package=THT]
  R12 = Resistor [tolerance=±5% resistance=270 package=THT]
  R13 = Resistor [tolerance=±5% resistance=270 package=THT]
  Buzzer = Piezo Speaker
  SG90 = Basic Servo
  LDR = Photocell (LDR) [package=THT]
  R15 = Resistor [tolerance=±5% resistance=4.7k package=THT]
  HC-SR04_Sensor_1 = HC-SR04 Ultrasonic Distance Sensor
  R16 = Resistor [tolerance=±5% resistance=10k package=THT]
  LED4 = LED - 5mm [color="Red (633nm)" package="5 mm [THT]"]
  R17 = Rotary Potentiometer (Small) [maximum_resistance=100kΩ package=THT]
  Bauteil1 = ws2812b [package="smd 2812b"]

nets:
  GND: Nano.GND, S1.Pin_1, S1.Pin_2, S2.Pin_1, S2.Pin_2, R11.Pin_1, R12.Pin_1, R13.Pin_1, Buzzer.pin2, SG90.gnd, LDR.pin_0, HC-SR04_Sensor_1.GND, R17.leg1, Bauteil1.VSS
  N1: Nano.D2, LED2.anode
  N2: Nano.D3, LED3.anode
  N3: Nano.D4, LED4.anode
  N4: Nano.D6, SG90.pulse
  N5: Nano.D8, R16.Pin_0
  N6: Nano.D9, HC-SR04_Sensor_1.TRIG
  N7: Nano.D10, HC-SR04_Sensor_1.ECHO
  N8: Nano.D11/MOSI, Buzzer.pin1
  5V: Nano.5V, SG90.vcc, R15.Pin_1, HC-SR04_Sensor_1.VCC, R17.leg2, Bauteil1.VDD
  N9: Nano.A5, LDR.pin_1, R15.Pin_0
  N10: Nano.A4, S2.Pin_3, S2.Pin_4
  N11: Nano.A1, S1.Pin_3, S1.Pin_4
  N12: Nano.A0, R17.wiper
  N13: LED2.cathode, R11.Pin_0
  N14: LED3.cathode, R12.Pin_0
  N15: R13.Pin_0, LED4.cathode
  N16: R16.Pin_1, Bauteil1.DIN
